# Fritzing sketch temperature (saved by Fritzing 0.9.3b)
circuit board: 3.95974cm x 4.70068cm
breadboards: 1

parts:
  Part1 = Arduino Nano (Rev3.0)
  BMP280_Breakout1 = BMP280 Breakout Board [part_number=BMP280]
  Part2 = NRF24L01+ Breakout Board
  JP1 = Header 2 [package=molex-1x2_lock]

nets:
  GND: Part1.GND, BMP280_Breakout1.GND, Part2.GND, JP1.1
  N1: Part1.D2, BMP280_Breakout1.SDO
  N2: Part1.D3, BMP280_Breakout1.CSB
  N3: Part1.D4, BMP280_Breakout1.SDA
  N4: Part1.D5, BMP280_Breakout1.SCL
  N5: Part1.D9, Part2.CE
  N6: Part1.D10, Part2.CS
  N7: Part1.D11/MOSI, Part2.MOSI
  N8: Part1.D12/MISO, Part2.MISO
  N9: Part1.VIN, JP1.2
  5V: Part1.5V, BMP280_Breakout1.VCC
  3V3: Part1.3V3, Part2.VCC
  N10: Part1.D13/SCK, Part2.SCK

notes:
  arduino nano v3.0
  NRF24L01+
  bmp280
  temperature sensor v0.1

custom parts:
  BMP280 Breakout Board: This is a breakout board for the Bosch Sensortec BMP280, "an absolute barometric pressure sensor especially designed for mobile applications." The operation range is 300 to 1100 hPa. Supply voltage is 1.2 to 3.6V. Operating temperature range is -40 to +85 °C.

// code stored in the sketch: HumiditySensorHA.ino
/**
 * The MySensors Arduino library handles the wireless radio link and protocol
 * between your home built sensors/actuators and HA controller of choice.
 * The sensors forms a self healing radio network with optional repeaters. Each
 * repeater and gateway builds a routing tables in EEPROM which keeps track of the
 * network topology allowing messages to be routed to nodes.
 *
 * Created by Henrik Ekblad <henrik.ekblad@mysensors.org>
 * Copyright (C) 2013-2015 Sensnology AB
 * Full contributor list: https://github.com/mysensors/Arduino/graphs/contributors
 *
 * Documentation: http://www.mysensors.org
 * Support Forum: http://forum.mysensors.org
 *
 * This program is free software; you can redistribute it and/or
 * modify it under the terms of the GNU General Public License
 * version 2 as published by the Free Software Foundation.
 *
 *******************************
 *
 * REVISION HISTORY
 * Version 1.0: Henrik EKblad
 * Version 1.1 - 2016-07-20: Converted to MySensors v2.0 and added various improvements - Torben Woltjen (mozzbozz)
 * 
 * DESCRIPTION
 * This sketch provides an example of how to implement a humidity/temperature
 * sensor using a DHT11/DHT-22.
 *  
 * For more information, please visit:
 * http://www.mysensors.org/build/humidity
 * 
 */

// Enable debug prints
#define MY_DEBUG

// Enable and select radio type attached 
#define MY_RADIO_NRF24
//#define MY_RADIO_RFM69
//#define MY_RS485

#define MY_BAUD_RATE 9600

// Set this to the pin you connected the DHT's data pin to
#define DHT_DATA_PIN 16

#define BMP_SCK 5
#define BMP_MOSI 4 
#define BMP_CS 3
#define BMP_MISO 2


// Set this offset if the sensor has a permanent small offset to the real temperatures
#define SENSOR_TEMP_OFFSET 0

// Sleep time between sensor updates (in milliseconds)
// Must be >1000ms for DHT22 and >2000ms for DHT11
static const uint64_t UPDATE_INTERVAL = 200000;

// Force sending an update of the temperature after n sensor reads, so a controller showing the
// timestamp of the last update doesn't show something like 3 hours in the unlikely case, that
// the value didn't change since;
// i.e. the sensor would force sending an update every UPDATE_INTERVAL*FORCE_UPDATE_N_READS [ms]
static const uint8_t FORCE_UPDATE_N_READS = 10;

#define MY_NODE_ID 1
#define CHILD_ID_TEMP 1

float lastTemp;
float lastHum;
uint8_t nNoUpdatesTemp;
uint8_t nNoUpdatesHum;


#include <SPI.h>
#include <Wire.h>
#include <MySensors.h>  
#include <Adafruit_BMP280.h>

MyMessage msgTemp(CHILD_ID_TEMP, V_TEMP);
Adafruit_BMP280 bmp(BMP_CS, BMP_MOSI, BMP_MISO,  BMP_SCK);


void presentation()  
{ 
  // Send the sketch version information to the gateway
  sendSketchInfo("Temperature", "1.1");

  // Register all sensors to gw (they will be created as child devices)
  present(CHILD_ID_TEMP, S_TEMP);
}


void setup()
{
  if (!bmp.begin()) {  
    Serial.println("Could not find a valid BMP280 sensor, check wiring!");
    while (1);
  }

}


void loop()      
{
  
  float temperature = (bmp.readTemperature() - 4.95);
  send(msgTemp.set(temperature, 1));

  #ifdef MY_DEBUG
  Serial.print("T: ");
  Serial.println(temperature);
  #endif

  sleep(UPDATE_INTERVAL);
}
