# Fritzing sketch led_strip (saved by Fritzing 0.9.3b)
circuit board: 3.96cm x 4.7cm
breadboards: 1

parts:
  Q1 = Basic FET N-Channel [package="TO220 [THT]"]
  Part2 = NRF24L01+ Breakout Board
  JP1 = Header 2 [package=jst-2-pth]
  Part4 = Infra red receiver
  JP3 = Header 2 [package=molex-1x2_lock]
  JP2 = Header 2 [package=jst-2-pth]
  Part1 = Arduino Nano (Rev3.0)

nets:
  N1: Q1.gate, Part1.D5
  N2: Q1.drain, JP1.2
  GND: Q1.source, Part2.GND, Part4.GND, JP3.1, JP2.2, Part1.GND
  VCC: Part2.VCC, Part1.3V3
  N3: Part2.CE, Part1.D9
  N4: Part2.CS, Part1.D10
  N5: Part2.SCK, Part1.D13/SCK
  N6: Part2.MOSI, Part1.D11/MOSI
  N7: Part2.MISO, Part1.D12/MISO
  N8: JP1.1, JP3.2, JP2.1, Part1.VIN
  VCC_2: Part4.VCC, Part1.5V
  N9: Part4.Data, Part1.D6

notes:
  led strip
  power supply
  led strip driver v0.1
  NRF24L01+
  arduino nano v3.0
  in
  led

// code stored in the sketch: LedStrip.ino
// Enable debug prints to serial monitor
#define MY_DEBUG

// Enable and select radio type attached
#define MY_RADIO_NRF24

#define MY_BAUD_RATE 9600
#define MY_NODE_ID 3
#define CHILD_ID_TEMP 3
bool initialValueSent = false;

#include <MySensors.h>
#include <IRremote.h>

#define FADE_SPEED 5    // make this higher to slow down
#define IR_PIN 5        // input pin for IR sensor
#define LED_PIN 5       // pin number of the fet driver
#define LED_ON 1        // GPIO value to write to turn on attached relay
#define LED_OFF 0       // GPIO value to write to turn off attached relay

int actualValue; 				//actual value of the led strip output

#define MAX_VALUE 255
#define MIN_VALUE 0

MyMessage msg(CHILD_ID_TEMP, V_STATUS);
IRrecv irrecv(IR_PIN);
decode_results signals;


void before()
{
}

void setup() {
    
  // set led driver pin to output mode
  pinMode(LED_PIN, OUTPUT);
  // Set relay to last known state (using eeprom storage)
  digitalWrite(LED_PIN, LED_OFF);
  actualValue = 0;
  
  Serial.println("Sending initial value");
  send(msg.set(LED_OFF));
  Serial.println("Requesting initial value from controller");
  request(CHILD_ID_TEMP, V_STATUS);
  wait(2000, C_SET, V_STATUS);
    
  irrecv.enableIRIn(); // enable input from IR receiver
}

void presentation()
{
    // Send the sketch version information to the gateway and Controller
    sendSketchInfo("Led strip", "1.0");

    // Register all sensors to gw (they will be created as child devices)
    present(CHILD_ID_TEMP, S_BINARY);
}
 
 
void loop() {
    if (irrecv.decode(&signals)) {
        Serial.println(signals.value, HEX);
        if(signals.value == 0xFFA857){
            fadeTo(actualValue + 50);
        }
        else if (signals.value == 0xFFE01F){
            fadeTo(actualValue - 50);
        }
        irrecv.resume(); // get the next signal
    }
} 

void receive(const MyMessage &message)
{
    // We only expect one type of message from controller. But we better check anyway.
    if (message.type==V_STATUS) {
        // Store state in eeprom
        saveState(message.sensor, message.getBool());
        // Write some debug info
        Serial.print("Incoming change for sensor:");
        Serial.print(message.sensor);
        Serial.print(", New status: ");
        Serial.println(message.getBool());
        
        // Change relay state
        fadeTo(message.getBool()?MAX_VALUE:MIN_VALUE);
    }
}

void fadeTo(int fadeToValue) {
  if(fadeToValue <= MIN_VALUE){
    send(msg.set(LED_OFF));
    fadeToValue = MIN_VALUE;
  }
  else if(fadeToValue > MAX_VALUE){
    fadeToValue = MAX_VALUE;
  }
  else {
    send(msg.set(LED_ON));
  }
  
  while(actualValue != fadeToValue){
      actualValue < fadeToValue ? actualValue++ : actualValue--;
      analogWrite(LED_PIN, actualValue);
      delay(FADE_SPEED);
  }

}
